// Logisim project mainLaba8.circ as structural Verilog: 1 circuit, main circuit Гарвардская архитектура
module \Гарвардская_архитектура  (
);

  wire and_1_out, Click_out, not_1_out, RESET_out;
  wire [2:0] counter_1_q, ram_1_data;
  wire [7:0] adder_1_out, multiplexer_1_out, ram_2_data, register_1_q;

  Counter #(.width(3), .max('h7)) counter_1 (
    .Q(counter_1_q), .clk(Click_out), .clr(RESET_out));  // open: load, D, count, carry
  Button Click (.out(Click_out));
  Button RESET (.out(RESET_out));
  not not_1 (not_1_out, Click_out);
  RAM #(.addrWidth(3), .dataWidth(3), .bus("separate")) ram_1 (
    .addr(counter_1_q), .data(ram_1_data));  // open: din, str, sel, clk, ld, clr
  RAM #(.addrWidth(3), .bus("separate")) ram_2 (
    .addr(counter_1_q), .din(register_1_q), .data(ram_2_data), .clk(ram_1_data[1]));  // open: str, sel, ld, clr
  // Probe on ram_2_data
  // Probe on adder_1_out
  Adder adder_1 (.a(register_1_q), .b(ram_2_data), .out(adder_1_out));  // open: cin, cout
  and and_1 (and_1_out, ram_1_data[0], not_1_out);
  Register register_1 (.D(multiplexer_1_out), .Q(register_1_q), .clk(and_1_out));  // open: en, clr
  Multiplexer #(.width(8)) multiplexer_1 (
    .in0(adder_1_out), .in1(ram_2_data), .out(multiplexer_1_out), .sel(ram_1_data[2]));  // open: en
endmodule
